# Fritzing sketch layout (saved by Fritzing 0.8.3b)
breadboards: 1

parts:
  Left_Nob = Adafruit Gear-Reduced Stepper Motor (small)
  Right_Nob = Adafruit Gear-Reduced Stepper Motor (small)
  Part1 = Arduino Uno (Rev3)
  IC1 = ULN2803A [package=THT]

nets:
  N1: Left_Nob.RED, Right_Nob.RED, IC1.COM_-_Common
  N2: Left_Nob.ORANGE, IC1.Out_4
  N3: Left_Nob.YELLOW, IC1.Out_3
  N4: Left_Nob.PINK, IC1.Out_2
  N5: Left_Nob.BLUE, IC1.Out_1
  N6: Right_Nob.ORANGE, IC1.Out_8
  N7: Right_Nob.YELLOW, IC1.Out_7
  N8: Right_Nob.PINK, IC1.Out_6
  N9: Right_Nob.BLUE, IC1.Out_5
  N10: Part1.GND, IC1.0V
  N11: Part1.D8, IC1.In_4
  N12: Part1.D9_PWM, IC1.In_3
  N13: Part1.D10_PWM/SS, IC1.In_2
  N14: Part1.D11_PWM/MOSI, IC1.In_1
  N15: Part1.D4, IC1.In_8
  N16: Part1.D5_PWM, IC1.In_7
  N17: Part1.D6_PWM, IC1.In_6
  N18: Part1.D7, IC1.In_5

custom parts:
  Adafruit Gear-Reduced Stepper Motor (small): Adafruit gear-reduction stepper motor (small)
